// Logisim project BusTransfer.circ as structural Verilog: 2 circuits, main circuit main
module main (
  input  in_1,
  input  [1:0] in_2,
  input  [3:0] in_3,
  input  [3:0] in_4,
  input  [3:0] in_5,
  input  [3:0] in_6
);

  wire B1_out, B2_out, B3_out, B4_out, multiplexer_1_out, multiplexer_2_out, multiplexer_3_out,
       multiplexer_4_out;
  wire [3:0] R1_q, R2_q, R3_q, r4_q;

  Multiplexer #(.select(2)) multiplexer_1 (
    .in0(R1_q[0]), .in1(R2_q[0]), .in2(R3_q[0]), .in3(r4_q[0]), .out(multiplexer_1_out), .sel(in_2), .en(in_1));
  Button B1 (.out(B1_out));
  Register #(.width(4)) R1 (.D(in_3), .Q(R1_q), .clk(B1_out));  // open: en, clr
  Multiplexer #(.select(2)) multiplexer_2 (
    .in0(R1_q[1]), .in1(R2_q[1]), .in2(R3_q[1]), .in3(r4_q[1]), .out(multiplexer_2_out), .sel(in_2), .en(in_1));
  Register #(.width(4)) R2 (.D(in_4), .Q(R2_q), .clk(B2_out));  // open: en, clr
  Button B2 (.out(B2_out));
  Multiplexer #(.select(2)) multiplexer_3 (
    .in0(R1_q[2]), .in1(R2_q[2]), .in2(R3_q[2]), .in3(r4_q[2]), .out(multiplexer_3_out), .sel(in_2), .en(in_1));
  Button B3 (.out(B3_out));
  Register #(.width(4)) R3 (.D(in_5), .Q(R3_q), .clk(B3_out));  // open: en, clr
  Multiplexer #(.select(2)) multiplexer_4 (
    .in0(R1_q[3]), .in1(R2_q[3]), .in2(R3_q[3]), .in3(r4_q[3]), .out(multiplexer_4_out), .sel(in_2), .en(in_1));
  Register #(.width(4)) r4 (.D(in_6), .Q(r4_q), .clk(B4_out));  // open: en, clr
  Button B4 (.out(B4_out));
  LED led_1 (.in(multiplexer_1_out));
  LED led_2 (.in(multiplexer_2_out));
  LED led_3 (.in(multiplexer_3_out));
  LED led_4 (.in(multiplexer_4_out));
endmodule

module TwoBitBT (
  input  in_1,
  input  in_2,
  input  [1:0] in_3,
  input  [1:0] in_4
);

  wire clock_1_out, multiplexer_1_out, multiplexer_2_out;
  wire [1:0] register_1_q, register_2_q;

  Register #(.width(2)) register_1 (.D(in_3), .Q(register_1_q), .clk(clock_1_out));  // open: en, clr
  LED led_1 (.in(multiplexer_1_out));
  Multiplexer multiplexer_1 (
    .in0(register_1_q[1]), .in1(register_2_q[1]), .out(multiplexer_1_out), .sel(in_2), .en(in_1));
  Clock clock_1 (.out(clock_1_out));
  LED led_2 (.in(multiplexer_2_out));
  Multiplexer multiplexer_2 (
    .in0(register_1_q[0]), .in1(register_2_q[0]), .out(multiplexer_2_out), .sel(in_2), .en(in_1));
  Register #(.width(2)) register_2 (.D(in_4), .Q(register_2_q), .clk(clock_1_out));  // open: en, clr
endmodule
