// Logisim project LogicOperation.circ as structural Verilog: 1 circuit, main circuit main
module main (
  input  [3:0] in_1,
  input  [3:0] in_2,
  output [3:0] out_3
);

  wire [3:0] not_1_out;

  assign not_1_out = ~in_2;  // NOT_Gate not_1, 4 bits wide
  assign out_3 = in_1 & not_1_out;  // AND_Gate and_1, 4 bits wide
endmodule
