// Logisim project ThreeStateBuffer.circ as structural Verilog: 1 circuit, main circuit main
module main (
  input  [3:0] I0,
  input  [3:0] I1,
  input  [3:0] I2,
  input  [3:0] I3,
  input  [1:0] in_5,
  input  in_6,
  output [3:0] out_7
);

  wire B1_out, B2_out, B3_out, B4_out, decoder_1_out0, decoder_1_out1, decoder_1_out2, decoder_1_out3;
  wire [3:0] R0_2_q, R0_q, R2_q, R3_q;

  Register #(.width(4)) R0 (.D(I0), .Q(R0_q), .clk(B1_out));  // open: en, clr
  Button B1 (.out(B1_out));
  Register #(.width(4)) R0_2 (.D(I1), .Q(R0_2_q), .clk(B2_out));  // open: en, clr
  Button B2 (.out(B2_out));
  Button B3 (.out(B3_out));
  Register #(.width(4)) R2 (.D(I2), .Q(R2_q), .clk(B3_out));  // open: en, clr
  Register #(.width(4)) R3 (.D(I3), .Q(R3_q), .clk(B4_out));  // open: en, clr
  Button B4 (.out(B4_out));
  assign out_7 = decoder_1_out0 ? R0_q : 4'bz;  // Controlled_Buffer controlled_buffer_1
  Decoder #(.select(2)) decoder_1 (
    .out0(decoder_1_out0), .out1(decoder_1_out1), .out2(decoder_1_out2), .out3(decoder_1_out3), .sel(in_5),
    .en(in_6));
  assign out_7 = decoder_1_out1 ? R0_2_q : 4'bz;  // Controlled_Buffer controlled_buffer_2
  assign out_7 = decoder_1_out2 ? R2_q : 4'bz;  // Controlled_Buffer controlled_buffer_3
  assign out_7 = decoder_1_out3 ? R3_q : 4'bz;  // Controlled_Buffer controlled_buffer_4
endmodule
