// Logisim project MUX2x1.circ as structural Verilog: 1 circuit, main circuit main
module main (
  input  in_1,
  input  in_2,
  input  in_3,
  input  in_4,
  output out_5
);

  wire clock_1_out, register_1_q, register_2_q;

  Multiplexer multiplexer_1 (.in0(register_1_q), .in1(register_2_q), .out(out_5), .sel(in_2), .en(in_1));
  Register #(.width(1)) register_1 (.D(in_3), .Q(register_1_q), .clk(clock_1_out));  // open: en, clr
  Clock clock_1 (.out(clock_1_out));
  Register #(.width(1)) register_2 (.D(in_4), .Q(register_2_q), .clk(clock_1_out));  // open: en, clr
endmodule
