// Logisim project MUX4X2.circ as structural Verilog: 1 circuit, main circuit main
module main (
  input  in_1,
  input  in_2,
  input  [3:0] in_3,
  input  [3:0] in_4
);

  wire clock_1_out, clock_2_out, multiplexer_1_out, multiplexer_2_out, multiplexer_3_out, multiplexer_4_out;
  wire [3:0] register_1_q, register_2_q;

  Clock clock_1 (.out(clock_1_out));
  Multiplexer multiplexer_1 (
    .in0(register_1_q[3]), .in1(register_2_q[3]), .out(multiplexer_1_out), .sel(in_2), .en(in_1));
  Register #(.width(4)) register_1 (.D(in_3), .Q(register_1_q), .clk(clock_1_out));  // open: en, clr
  Multiplexer multiplexer_2 (
    .in0(register_1_q[2]), .in1(register_2_q[2]), .out(multiplexer_2_out), .sel(in_2), .en(in_1));
  Multiplexer multiplexer_3 (
    .in0(register_1_q[1]), .in1(register_2_q[1]), .out(multiplexer_3_out), .sel(in_2), .en(in_1));
  Multiplexer multiplexer_4 (
    .in0(register_1_q[0]), .in1(register_2_q[0]), .out(multiplexer_4_out), .sel(in_2), .en(in_1));
  Register #(.width(4)) register_2 (.D(in_4), .Q(register_2_q), .clk(clock_2_out));  // open: en, clr
  Clock clock_2 (.out(clock_2_out));
  LED led_1 (.in(multiplexer_1_out));
  LED led_2 (.in(multiplexer_2_out));
  LED led_3 (.in(multiplexer_3_out));
  LED led_4 (.in(multiplexer_4_out));
endmodule
